// Logisim project Befunge.circ as structural Verilog: 6 circuits, main circuit Befunge
module Befunge (
  input  Reset
);

  wire clock_1_out, outputcontrol_1_write_en;
  wire [3:0] numberdriver_1_out_2, numberdriver_1_out_3, numberdriver_1_out_4, numberdriver_1_out_5,
       numberdriver_1_out_6, numberdriver_1_out_7, numberdriver_1_out_8, numberdriver_1_out_9;
  wire [6:0] outputcontrol_1_ascii_out;
  wire [7:0] program_1_instr_out;
  wire [31:0] control_1_ctrl_out, control_1_stack_out, outputcontrol_1_number_out, stack_1_stack_out;

  Program program_1 (.Instr_OUT(program_1_instr_out), .Ctrl_IN(control_1_ctrl_out), .RESET(Reset));
  Control control_1 (
    .Instr_IN(program_1_instr_out), .Ctrl_OUT(control_1_ctrl_out), .Stack_OUT(control_1_stack_out),
    .Stack_IN(stack_1_stack_out), .Reset(Reset));
  Stack stack_1 (
    .Stack_IN(control_1_stack_out), .Stack_OUT(stack_1_stack_out), .Ctrl_IN(control_1_ctrl_out), .Reset(Reset));
  NumberDriver numberdriver_1 (
    .in_1(outputcontrol_1_number_out), .out_2(numberdriver_1_out_2), .out_3(numberdriver_1_out_3),
    .out_4(numberdriver_1_out_4), .out_5(numberdriver_1_out_5), .out_6(numberdriver_1_out_6),
    .out_7(numberdriver_1_out_7), .out_8(numberdriver_1_out_8), .out_9(numberdriver_1_out_9));
  Hex_Digit_Display hex_digit_display_1 (.value(numberdriver_1_out_2));  // open: dp
  Clock clock_1 (.out(clock_1_out));
  OutputControl outputcontrol_1 (
    .Stack_IN(stack_1_stack_out), .Ctrl_IN(control_1_ctrl_out), .ASCII_OUT(outputcontrol_1_ascii_out),
    .Write_EN(outputcontrol_1_write_en), .Number_OUT(outputcontrol_1_number_out));
  TTY #(.rows(23), .cols(48)) tty_1 (
    .data(outputcontrol_1_ascii_out), .clk(clock_1_out), .we(outputcontrol_1_write_en), .clr(Reset));
  Hex_Digit_Display hex_digit_display_2 (.value(numberdriver_1_out_4));  // open: dp
  Hex_Digit_Display hex_digit_display_3 (.value(numberdriver_1_out_3));  // open: dp
  Hex_Digit_Display hex_digit_display_4 (.value(numberdriver_1_out_5));  // open: dp
  Hex_Digit_Display hex_digit_display_5 (.value(numberdriver_1_out_6));  // open: dp
  Hex_Digit_Display hex_digit_display_6 (.value(numberdriver_1_out_8));  // open: dp
  Hex_Digit_Display hex_digit_display_7 (.value(numberdriver_1_out_7));  // open: dp
  Hex_Digit_Display hex_digit_display_8 (.value(numberdriver_1_out_9));  // open: dp
endmodule

// STACK
module Stack (
  input  Reset,
  input  [31:0] Stack_IN,
  input  [31:0] Ctrl_IN,
  output [31:0] Stack_OUT
);

  wire clock_1_out, not_1_out, or_1_out;
  wire [23:0] adder_1_out, controlled_buffer_1_out, controlled_buffer_3_out, register_1_q, subtractor_1_out;

  assign controlled_buffer_1_out = Ctrl_IN[16] ? adder_1_out : 24'bz;  // Controlled_Buffer controlled_buffer_1
  assign controlled_buffer_1_out = Ctrl_IN[15] ? subtractor_1_out : 24'bz;  // Controlled_Buffer controlled_buffer_2
  or or_1 (or_1_out, Ctrl_IN[15], Ctrl_IN[16]);
  Adder #(.width(24)) adder_1 (.a(register_1_q), .b(24'h1), .out(adder_1_out));  // open: cin, cout
  Subtractor #(.width(24)) subtractor_1 (.a(register_1_q), .b(24'h1), .out(subtractor_1_out));  // open: bin, bout
  assign controlled_buffer_3_out = not_1_out ? register_1_q : 24'bz;  // Controlled_Buffer controlled_buffer_3
  Register #(.width(24)) register_1 (
    .D(controlled_buffer_1_out), .en(or_1_out), .Q(register_1_q), .clk(clock_1_out), .clr(Reset));
  not not_1 (not_1_out, Ctrl_IN[15]);
  assign controlled_buffer_3_out = Ctrl_IN[15] ? subtractor_1_out : 24'bz;  // Controlled_Buffer controlled_buffer_4
  Clock clock_1 (.out(clock_1_out));
  RAM #(.addrWidth(24), .dataWidth(32), .bus("separate")) ram_1 (
    .addr(controlled_buffer_3_out), .din(Stack_IN), .data(Stack_OUT), .str(Ctrl_IN[16]), .clk(clock_1_out),
    .ld(Ctrl_IN[15]));  // open: sel, clr

  // Notes on the sheet:
  //   PUSH
  //   POP
endmodule

// PROG
module Program (
  input  RESET,
  input  [31:0] Ctrl_IN,
  output [7:0] Instr_OUT
);

  wire clock_1_out, controlled_buffer_2_out, nor_1_out, nor_2_out, not_1_out, not_2_out, or_1_out, or_2_out,
       or_3_out;
  wire [3:0] controlled_buffer_1_out, Dir_q, pull_resistor_1_node;
  wire [11:0] adder_1_out, adder_2_out, bit_extender_1_out, controlled_buffer_5_out, controlled_buffer_6_out,
       controlled_buffer_10_out, controlled_buffer_12_out, subtractor_1_out, subtractor_2_out, X_q, Y_q;

  assign controlled_buffer_1_out = RESET ? 4'b0001 : 4'bz;  // Controlled_Buffer controlled_buffer_1
  assign controlled_buffer_2_out = RESET ? 1'b1 : 1'bz;  // Controlled_Buffer controlled_buffer_2
  assign controlled_buffer_2_out = not_1_out ? Ctrl_IN[5] : 1'bz;  // Controlled_Buffer controlled_buffer_3
  not not_1 (not_1_out, RESET);
  assign controlled_buffer_1_out = not_1_out ? Ctrl_IN[4:1] : 4'bz;  // Controlled_Buffer controlled_buffer_4
  assign bit_extender_1_out = {{4{1'b0}}, Ctrl_IN[13:6]};  // Bit_Extender bit_extender_1
  nor nor_1 (nor_1_out, pull_resistor_1_node[0], pull_resistor_1_node[1]);
  assign controlled_buffer_5_out = nor_1_out ? bit_extender_1_out : 12'bz;  // Controlled_Buffer controlled_buffer_5
  nor nor_2 (nor_2_out, pull_resistor_1_node[2], pull_resistor_1_node[3]);
  assign controlled_buffer_6_out = nor_2_out ? bit_extender_1_out : 12'bz;  // Controlled_Buffer controlled_buffer_6
  Register #(.width(4), .trigger("high")) Dir (
    .D(controlled_buffer_1_out), .en(controlled_buffer_2_out), .Q(Dir_q), .clk(or_1_out));  // open: clr
  Pull_Resistor pull_resistor_1 (.node(pull_resistor_1_node));
  assign pull_resistor_1_node = Ctrl_IN[0] ? Dir_q : 4'bz;  // Controlled_Buffer controlled_buffer_7
  or or_1 (or_1_out, RESET, clock_1_out);
  or or_2 (or_2_out, pull_resistor_1_node[0], pull_resistor_1_node[1]);
  or or_3 (or_3_out, pull_resistor_1_node[2], pull_resistor_1_node[3]);
  Clock clock_1 (.out(clock_1_out));
  Register #(.width(12), .trigger("falling")) X (
    .D(controlled_buffer_5_out), .en(or_2_out), .Q(X_q), .clk(clock_1_out), .clr(RESET));
  assign controlled_buffer_5_out = or_2_out ? controlled_buffer_12_out : 12'bz;  // Controlled_Buffer controlled_buffer_8
  assign controlled_buffer_6_out = or_3_out ? controlled_buffer_12_out : 12'bz;  // Controlled_Buffer controlled_buffer_9
  Register #(.width(12), .trigger("falling")) Y (
    .D(controlled_buffer_6_out), .en(or_3_out), .Q(Y_q), .clk(clock_1_out), .clr(RESET));
  not not_2 (not_2_out, Ctrl_IN[31]);
  assign controlled_buffer_10_out = Ctrl_IN[31] ? 12'h2 : 12'bz;  // Controlled_Buffer controlled_buffer_10
  assign controlled_buffer_10_out = not_2_out ? 12'h1 : 12'bz;  // Controlled_Buffer controlled_buffer_11
  Adder #(.width(12)) adder_1 (.a(X_q), .b(controlled_buffer_10_out), .out(adder_1_out));  // open: cin, cout
  assign controlled_buffer_12_out = pull_resistor_1_node[0] ? adder_1_out : 12'bz;  // Controlled_Buffer controlled_buffer_12
  Adder #(.width(12)) adder_2 (.a(Y_q), .b(controlled_buffer_10_out), .out(adder_2_out));  // open: cin, cout
  assign controlled_buffer_12_out = pull_resistor_1_node[2] ? adder_2_out : 12'bz;  // Controlled_Buffer controlled_buffer_13
  Subtractor #(.width(12)) subtractor_1 (
    .a(X_q), .b(controlled_buffer_10_out), .out(subtractor_1_out));  // open: bin, bout
  assign controlled_buffer_12_out = pull_resistor_1_node[1] ? subtractor_1_out : 12'bz;  // Controlled_Buffer controlled_buffer_14
  Subtractor #(.width(12)) subtractor_2 (
    .a(Y_q), .b(controlled_buffer_10_out), .out(subtractor_2_out));  // open: bin, bout
  assign controlled_buffer_12_out = pull_resistor_1_node[3] ? subtractor_2_out : 12'bz;  // Controlled_Buffer controlled_buffer_15
  RAM #(.addrWidth(24), .bus("separate")) ram_1 (
    .addr({Y_q, X_q}), .din(Ctrl_IN[13:6]), .data(Instr_OUT), .str(Ctrl_IN[14]), .clk(clock_1_out));  // open: sel, ld, clr

  // Notes on the sheet:
  //   Dir-IN
  //   Dir-EN
  //   Next-Instr
  //   Put
endmodule

// CONTROL
module Control (
  input  [7:0] Instr_IN,
  input  Reset,
  input  [31:0] Stack_IN,
  output [31:0] Stack_OUT,
  output [31:0] Ctrl_OUT
);

  wire and_1_out, and_2_out, clock_1_out, clock_2_out, clock_3_out, clock_4_out, clock_5_out,
       comparator_1_eq, comparator_2_eq, comparator_3_eq, comparator_4_eq, comparator_5_eq, comparator_6_eq,
       comparator_7_eq, comparator_8_eq, comparator_9_eq, comparator_10_eq, comparator_11_eq,
       comparator_12_eq, comparator_13_eq, comparator_14_eq, comparator_15_eq, comparator_16_eq,
       comparator_17_eq, comparator_18_eq, comparator_19_eq, comparator_20_eq, comparator_21_eq,
       comparator_22_eq, comparator_23_eq, comparator_24_eq, comparator_25_eq, comparator_26_eq,
       comparator_27_eq, comparator_28_eq, comparator_29_eq, comparator_30_eq, comparator_31_eq,
       comparator_32_eq, comparator_33_eq, comparator_34_eq, comparator_35_gt, decoder_1_out1,
       decoder_1_out2, decoder_1_out3, decoder_1_out4, decoder_1_out5, decoder_1_out6, decoder_1_out7,
       decoder_1_out8, decoder_1_out9, decoder_1_out10, decoder_1_out11, decoder_1_out12, not_1_out,
       not_2_out, not_3_out, not_4_out, or_1_out, t_ff_1_q;
  wire [1:0] random_1_out;
  wire [3:0] rom_1_data_2;
  wire [7:0] adder_1_out, controlled_buffer_1_out, controlled_buffer_32_out, counter_1_q, register_1_q;
  wire [31:0] adder_2_out, bit_extender_1_out, bit_extender_2_out, bit_extender_3_out, bit_extender_4_out,
       controlled_buffer_34_out, controlled_buffer_45_out, divider_1_out, divider_2_rem, multiplier_1_out,
       pull_resistor_6_node, pull_resistor_7_node, R0_q, R1_q, rom_1_data, subtractor_1_out, undriven,
       undriven_2, undriven_3;

  Register #(.trigger("high")) register_1 (
    .D(Instr_IN), .en(rom_1_data[0]), .Q(register_1_q), .clk(or_1_out), .clr(Reset));
  or or_1 (or_1_out, clock_1_out, comparator_22_eq);
  Clock clock_1 (.out(clock_1_out));
  Comparator comparator_1 (.a(register_1_q), .b(8'h30), .eq(comparator_1_eq));  // open: gt, lt
  Comparator comparator_2 (.a(register_1_q), .b(8'h31), .eq(comparator_2_eq));  // open: gt, lt
  Comparator comparator_3 (.a(register_1_q), .b(8'h32), .eq(comparator_3_eq));  // open: gt, lt
  Comparator comparator_4 (.a(register_1_q), .b(8'h33), .eq(comparator_4_eq));  // open: gt, lt
  Comparator comparator_5 (.a(register_1_q), .b(8'h34), .eq(comparator_5_eq));  // open: gt, lt
  Comparator comparator_6 (.a(register_1_q), .b(8'h35), .eq(comparator_6_eq));  // open: gt, lt
  Comparator comparator_7 (.a(register_1_q), .b(8'h36), .eq(comparator_7_eq));  // open: gt, lt
  Comparator comparator_8 (.a(register_1_q), .b(8'h37), .eq(comparator_8_eq));  // open: gt, lt
  Comparator comparator_9 (.a(register_1_q), .b(8'h38), .eq(comparator_9_eq));  // open: gt, lt
  Comparator comparator_10 (.a(register_1_q), .b(8'h39), .eq(comparator_10_eq));  // open: gt, lt
  Comparator comparator_11 (.a(register_1_q), .b(8'h2b), .eq(comparator_11_eq));  // open: gt, lt
  Comparator comparator_12 (.a(register_1_q), .b(8'h2d), .eq(comparator_12_eq));  // open: gt, lt
  Comparator comparator_13 (.a(register_1_q), .b(8'h2a), .eq(comparator_13_eq));  // open: gt, lt
  Comparator comparator_14 (.a(register_1_q), .b(8'h2f), .eq(comparator_14_eq));  // open: gt, lt
  Comparator comparator_15 (.a(register_1_q), .b(8'h25), .eq(comparator_15_eq));  // open: gt, lt
  Comparator comparator_16 (.a(register_1_q), .b(8'h21), .eq(comparator_16_eq));  // open: gt, lt
  Comparator comparator_17 (.a(register_1_q), .b(8'h60), .eq(comparator_17_eq));  // open: gt, lt
  Comparator comparator_18 (.a(register_1_q), .b(8'h3e), .eq(comparator_18_eq));  // open: gt, lt
  Comparator comparator_19 (.a(register_1_q), .b(8'h3c), .eq(comparator_19_eq));  // open: gt, lt
  Comparator comparator_20 (.a(register_1_q), .b(8'h5e), .eq(comparator_20_eq));  // open: gt, lt
  Comparator comparator_21 (.a(register_1_q), .b(8'h76), .eq(comparator_21_eq));  // open: gt, lt
  Comparator comparator_22 (.a(register_1_q), .b(8'h3f), .eq(comparator_22_eq));  // open: gt, lt
  Comparator comparator_23 (.a(register_1_q), .b(8'h5f), .eq(comparator_23_eq));  // open: gt, lt
  Comparator comparator_24 (.a(register_1_q), .b(8'h7c), .eq(comparator_24_eq));  // open: gt, lt
  Comparator comparator_25 (.a(register_1_q), .b(8'h3a), .eq(comparator_25_eq));  // open: gt, lt
  Comparator comparator_26 (.a(register_1_q), .b(8'h5c), .eq(comparator_26_eq));  // open: gt, lt
  Comparator comparator_27 (.a(register_1_q), .b(8'h24), .eq(comparator_27_eq));  // open: gt, lt
  Comparator comparator_28 (.a(register_1_q), .b(8'h2c), .eq(comparator_28_eq));  // open: gt, lt
  Comparator comparator_29 (.a(register_1_q), .b(8'h2e), .eq(comparator_29_eq));  // open: gt, lt
  Comparator comparator_30 (.a(register_1_q), .b(8'h23), .eq(comparator_30_eq));  // open: gt, lt
  Comparator comparator_31 (.a(register_1_q), .b(8'h40), .eq(comparator_31_eq));  // open: gt, lt
  assign controlled_buffer_1_out = comparator_1_eq ? 8'h1 : 8'bz;  // Controlled_Buffer controlled_buffer_1
  assign controlled_buffer_1_out = comparator_2_eq ? 8'h2 : 8'bz;  // Controlled_Buffer controlled_buffer_2
  assign controlled_buffer_1_out = comparator_3_eq ? 8'h3 : 8'bz;  // Controlled_Buffer controlled_buffer_3
  assign controlled_buffer_1_out = comparator_4_eq ? 8'h4 : 8'bz;  // Controlled_Buffer controlled_buffer_4
  assign controlled_buffer_1_out = comparator_5_eq ? 8'h5 : 8'bz;  // Controlled_Buffer controlled_buffer_5
  assign controlled_buffer_1_out = comparator_6_eq ? 8'h6 : 8'bz;  // Controlled_Buffer controlled_buffer_6
  assign controlled_buffer_1_out = comparator_7_eq ? 8'h7 : 8'bz;  // Controlled_Buffer controlled_buffer_7
  assign controlled_buffer_1_out = comparator_8_eq ? 8'h8 : 8'bz;  // Controlled_Buffer controlled_buffer_8
  assign controlled_buffer_1_out = comparator_9_eq ? 8'h9 : 8'bz;  // Controlled_Buffer controlled_buffer_9
  assign controlled_buffer_1_out = comparator_10_eq ? 8'ha : 8'bz;  // Controlled_Buffer controlled_buffer_10
  assign controlled_buffer_1_out = comparator_11_eq ? 8'hb : 8'bz;  // Controlled_Buffer controlled_buffer_11
  assign controlled_buffer_1_out = comparator_12_eq ? 8'hf : 8'bz;  // Controlled_Buffer controlled_buffer_12
  assign controlled_buffer_1_out = comparator_13_eq ? 8'h13 : 8'bz;  // Controlled_Buffer controlled_buffer_13
  assign controlled_buffer_1_out = comparator_14_eq ? 8'h17 : 8'bz;  // Controlled_Buffer controlled_buffer_14
  assign controlled_buffer_1_out = comparator_15_eq ? 8'h1b : 8'bz;  // Controlled_Buffer controlled_buffer_15
  assign controlled_buffer_1_out = comparator_16_eq ? 8'h1f : 8'bz;  // Controlled_Buffer controlled_buffer_16
  assign controlled_buffer_1_out = comparator_17_eq ? 8'h22 : 8'bz;  // Controlled_Buffer controlled_buffer_17
  assign controlled_buffer_1_out = comparator_18_eq ? 8'h26 : 8'bz;  // Controlled_Buffer controlled_buffer_18
  assign controlled_buffer_1_out = comparator_19_eq ? 8'h27 : 8'bz;  // Controlled_Buffer controlled_buffer_19
  assign controlled_buffer_1_out = comparator_20_eq ? 8'h28 : 8'bz;  // Controlled_Buffer controlled_buffer_20
  assign controlled_buffer_1_out = comparator_21_eq ? 8'h29 : 8'bz;  // Controlled_Buffer controlled_buffer_21
  assign controlled_buffer_1_out = comparator_22_eq ? 8'h2a : 8'bz;  // Controlled_Buffer controlled_buffer_22
  assign controlled_buffer_1_out = comparator_23_eq ? 8'h2b : 8'bz;  // Controlled_Buffer controlled_buffer_23
  assign controlled_buffer_1_out = comparator_24_eq ? 8'h2e : 8'bz;  // Controlled_Buffer controlled_buffer_24
  assign controlled_buffer_1_out = comparator_25_eq ? 8'h31 : 8'bz;  // Controlled_Buffer controlled_buffer_25
  assign controlled_buffer_1_out = comparator_26_eq ? 8'h35 : 8'bz;  // Controlled_Buffer controlled_buffer_26
  assign controlled_buffer_1_out = comparator_27_eq ? 8'h3a : 8'bz;  // Controlled_Buffer controlled_buffer_27
  assign controlled_buffer_1_out = comparator_28_eq ? 8'h3b : 8'bz;  // Controlled_Buffer controlled_buffer_28
  assign controlled_buffer_1_out = comparator_29_eq ? 8'h3c : 8'bz;  // Controlled_Buffer controlled_buffer_29
  assign controlled_buffer_1_out = comparator_30_eq ? 8'h3d : 8'bz;  // Controlled_Buffer controlled_buffer_30
  assign controlled_buffer_1_out = comparator_31_eq ? 8'h3e : 8'bz;  // Controlled_Buffer controlled_buffer_31
  Pull_Resistor pull_resistor_1 (.node(controlled_buffer_1_out));
  not not_1 (not_1_out, t_ff_1_q);
  assign controlled_buffer_32_out = not_1_out ? controlled_buffer_1_out : 8'bz;  // Controlled_Buffer controlled_buffer_32
  not not_2 (not_2_out, comparator_32_eq);
  Comparator comparator_32 (.a(register_1_q), .b(8'h22), .eq(comparator_32_eq));  // open: gt, lt
  Clock clock_2 (.out(clock_2_out));
  Comparator comparator_33 (.a(register_1_q), .b(8'h22), .eq(comparator_33_eq));  // open: gt, lt
  Counter counter_1 (
    .load(rom_1_data[0]), .D({8{1'b0}}), .count(not_3_out), .Q(counter_1_q), .clk(and_1_out), .clr(Reset));  // open: carry
  and and_1 (and_1_out, clock_3_out, not_4_out);
  not not_3 (not_3_out, rom_1_data[0]);
  not not_4 (not_4_out, rom_1_data[17]);
  Clock clock_3 (.out(clock_3_out));
  assign bit_extender_1_out = {{24{1'b0}}, register_1_q};  // Bit_Extender bit_extender_1
  T_Flip_Flop #(.trigger("falling")) t_ff_1 (
    .clk(clock_2_out), .T(comparator_33_eq), .Q(t_ff_1_q));  // open: Qn, preset, reset, en
  Adder adder_1 (.a(counter_1_q), .b(controlled_buffer_32_out), .out(adder_1_out));  // open: cin, cout
  and and_2 (and_2_out, not_2_out, t_ff_1_q);
  assign Stack_OUT = and_2_out ? bit_extender_1_out : 32'bz;  // Controlled_Buffer controlled_buffer_33
  assign controlled_buffer_34_out = and_2_out ? 32'h10001 : 32'bz;  // Controlled_Buffer controlled_buffer_34
  Decoder #(.select(4)) decoder_1 (
    .out1(decoder_1_out1), .out2(decoder_1_out2), .out3(decoder_1_out3), .out4(decoder_1_out4),
    .out5(decoder_1_out5), .out6(decoder_1_out6), .out7(decoder_1_out7), .out8(decoder_1_out8),
    .out9(decoder_1_out9), .out10(decoder_1_out10), .out11(decoder_1_out11), .out12(decoder_1_out12),
    .sel(rom_1_data_2));  // open: out0, out13, out14, out15, en
  Pull_Resistor pull_resistor_2 (.node(Stack_OUT));
  Pull_Resistor pull_resistor_3 (.node(controlled_buffer_34_out));
  ROM #(.dataWidth(32)) rom_1 (
    .addr(adder_1_out), .data({rom_1_data[31:29], rom_1_data_2, rom_1_data[24:0]}));  // open: sel
  Pull_Resistor pull_resistor_4 (.node({rom_1_data[31:29], rom_1_data_2, rom_1_data[24:0]}));
  assign bit_extender_2_out = {{28{1'b0}}, rom_1_data[21:18]};  // Bit_Extender bit_extender_2
  assign Ctrl_OUT = pull_resistor_7_node | {rom_1_data[31:29], rom_1_data_2, rom_1_data[24:0]} | controlled_buffer_34_out | controlled_buffer_45_out | pull_resistor_6_node;  // OR_Gate or_2, 32 bits wide
  assign Stack_OUT = rom_1_data[22] ? bit_extender_2_out : 32'bz;  // Controlled_Buffer controlled_buffer_35
  assign Stack_OUT = decoder_1_out1 ? adder_2_out : 32'bz;  // Controlled_Buffer controlled_buffer_36
  assign Stack_OUT = decoder_1_out2 ? subtractor_1_out : 32'bz;  // Controlled_Buffer controlled_buffer_37
  assign Stack_OUT = decoder_1_out3 ? multiplier_1_out : 32'bz;  // Controlled_Buffer controlled_buffer_38
  assign Stack_OUT = decoder_1_out4 ? divider_1_out : 32'bz;  // Controlled_Buffer controlled_buffer_39
  assign Stack_OUT = decoder_1_out5 ? divider_2_rem : 32'bz;  // Controlled_Buffer controlled_buffer_40
  assign Stack_OUT = decoder_1_out6 ? bit_extender_3_out : 32'bz;  // Controlled_Buffer controlled_buffer_41
  assign Stack_OUT = decoder_1_out7 ? bit_extender_4_out : 32'bz;  // Controlled_Buffer controlled_buffer_42
  Clock clock_4 (.out(clock_4_out));
  assign Stack_OUT = decoder_1_out11 ? R0_q : 32'bz;  // Controlled_Buffer controlled_buffer_43
  assign Stack_OUT = decoder_1_out12 ? R1_q : 32'bz;  // Controlled_Buffer controlled_buffer_44
  Register #(.width(32)) R0 (.D(Stack_IN), .en(rom_1_data[23]), .Q(R0_q), .clk(clock_5_out));  // open: clr
  Register #(.width(32)) R1 (.D(Stack_IN), .en(rom_1_data[24]), .Q(R1_q), .clk(clock_5_out));  // open: clr
  Clock clock_5 (.out(clock_5_out));
  Adder #(.width(32)) adder_2 (.a(R1_q), .b(R0_q), .out(adder_2_out));  // open: cin, cout
  Subtractor #(.width(32)) subtractor_1 (.a(R1_q), .b(R0_q), .out(subtractor_1_out));  // open: bin, bout
  Multiplier #(.width(32)) multiplier_1 (.a(R1_q), .b(R0_q), .out(multiplier_1_out));  // open: cin, cout
  Divider #(.width(32)) divider_1 (.a(R1_q), .b(R0_q), .out(divider_1_out));  // open: upper, rem
  Divider #(.width(32)) divider_2 (.a(R1_q), .b(R0_q), .rem(divider_2_rem));  // open: out, upper
  Comparator #(.width(32), .mode("unsigned")) comparator_34 (
    .a(R0_q), .b({32{1'b0}}), .eq(comparator_34_eq));  // open: gt, lt
  Comparator #(.width(32), .mode("unsigned")) comparator_35 (
    .a(R1_q), .b(R0_q), .gt(comparator_35_gt));  // open: eq, lt
  Random #(.width(2)) random_1 (.clk(clock_4_out), .next(clock_4_out), .out(random_1_out));  // open: clr
  Decoder #(.select(2), .disabled(0)) decoder_2 (
    .out0(undriven[1]), .out1(undriven[2]), .out2(undriven[3]), .out3(undriven[4]), .sel(random_1_out));  // open: en
  assign controlled_buffer_45_out = decoder_1_out8 ? undriven : 32'bz;  // Controlled_Buffer controlled_buffer_45
  Pull_Resistor pull_resistor_5 (.node(controlled_buffer_45_out));
  not not_5 (undriven_2[2], undriven_2[1]);
  Comparator #(.width(32), .mode("unsigned")) comparator_36 (
    .a(R0_q), .b({32{1'b0}}), .eq(undriven_2[1]));  // open: gt, lt
  Pull_Resistor pull_resistor_6 (.node(pull_resistor_6_node));
  Comparator #(.width(32), .mode("unsigned")) comparator_37 (
    .a(R0_q), .b({32{1'b0}}), .eq(undriven_3[3]));  // open: gt, lt
  Pull_Resistor pull_resistor_7 (.node(pull_resistor_7_node));
  assign bit_extender_3_out = {{31{1'b0}}, comparator_34_eq};  // Bit_Extender bit_extender_3
  assign bit_extender_4_out = {{31{1'b0}}, comparator_35_gt};  // Bit_Extender bit_extender_4
  assign pull_resistor_6_node = decoder_1_out9 ? undriven_2 : 32'bz;  // Controlled_Buffer controlled_buffer_46
  not not_6 (undriven_3[4], undriven_3[3]);
  assign pull_resistor_7_node = decoder_1_out10 ? undriven_3 : 32'bz;  // Controlled_Buffer controlled_buffer_47

  // Notes on the sheet:
  //   0
  //   1
  //   2
  //   3
  //   4
  //   5
  //   6
  //   7
  //   8
  //   9
  //   +
  //   -
  //   *
  //   /
  //   %
  //   !
  //   `
  //   >
  //   <
  //   ^
  //   v
  //   ?
  //   _
  //   |
  //   :
  //   \
  //   $
  //   ,
  //   .
  //   #
  //   @
  //   contents of rom_1 (hex, n*v repeats v):
  //   1 410001 450001 490001 4d0001 510001 550001 590001 5d0001 610001 650001 808000 1008000 2010000 1
  //   808000 1008000 4010000 1 808000 1008000 6010000 1 808000 1008000 8010000 1 808000 1008000 a010000 1
  //   808000 c010000 1 808000 1008000 e010000 1 23 25 31 29 10000021 808000 12000020 1 808000 14000020 1
  //   808000 16010000 16010000 1 808000 1008000 16010000 18010000 1 8001 20008001 40008001 80000001 20000
endmodule

module OutputControl (
  input  [31:0] Stack_IN,
  input  [31:0] Ctrl_IN,
  output [31:0] Number_OUT,
  output [6:0] ASCII_OUT,
  output Write_EN
);

  wire clock_1_out;
  wire [6:0] bit_extender_1_out;

  Clock clock_1 (.out(clock_1_out));
  Register #(.width(32)) register_1 (.D(Stack_IN), .en(Ctrl_IN[30]), .Q(Number_OUT), .clk(clock_1_out));  // open: clr
  Bit_Extender #(.in_width(32), .out_width(7)) bit_extender_1 (.in(Stack_IN), .out(bit_extender_1_out));
  Pull_Resistor pull_resistor_1 (.node(ASCII_OUT));
  assign ASCII_OUT = Ctrl_IN[29] ? bit_extender_1_out : 7'bz;  // Controlled_Buffer controlled_buffer_1

  assign Write_EN = Ctrl_IN[29];
endmodule

module NumberDriver (
  input  [31:0] in_1,
  output [3:0] out_2,
  output [3:0] out_3,
  output [3:0] out_4,
  output [3:0] out_5,
  output [3:0] out_6,
  output [3:0] out_7,
  output [3:0] out_8,
  output [3:0] out_9
);


  assign out_2 = in_1[31:28];
  assign out_3 = in_1[27:24];
  assign out_4 = in_1[23:20];
  assign out_5 = in_1[19:16];
  assign out_6 = in_1[15:12];
  assign out_7 = in_1[11:8];
  assign out_8 = in_1[7:4];
  assign out_9 = in_1[3:0];
endmodule
